# Fritzing sketch Mesure Cur1 (saved by Fritzing 0.9.3b)

parts:
  R7 = 100 KΩ Resistor [package="0402 [SMD]"]
  R6 = 100 KΩ Resistor [package="0402 [SMD]"]
  R8 = 100 KΩ Resistor [package="0402 [SMD]"]
  IC1 = LM324 [package=dil16]
  R9 = 100 KΩ Resistor [package="0402 [SMD]"]

nets:
  Battery -: R7.Pin_0
  N1: R7.Pin_1, R6.Pin_0, IC1.IN1+
  GND: R6.Pin_1, R9.Pin_0
  N2: R8.Pin_0, IC1.IN1-, R9.Pin_1
  N3: R8.Pin_1, IC1.OUT1

custom parts:
  100 KΩ Resistor: Resistor Basic schematic elements and footprints for 0603, 1206, and PTH resistors.
  LM324: LM324 Quad OpAmp
