# Fritzing sketch Mesure Cur2 (saved by Fritzing 0.9.3b)

parts:
  R23 = 100 KΩ Resistor [package="0402 [SMD]"]
  IC1 = LM324 [package=dil16]
  R24 = 100 KΩ Resistor [package="0402 [SMD]"]

nets:
  N1: R23.Pin_0, IC1.IN1-, R24.Pin_1
  N2: R23.Pin_1, IC1.OUT1
  GND: IC1.IN1+
  curr_measur_1: R24.Pin_0

custom parts:
  100 KΩ Resistor: Resistor Basic schematic elements and footprints for 0603, 1206, and PTH resistors.
  LM324: LM324 Quad OpAmp
