# Fritzing sketch Mesure Vol1 (saved by Fritzing 0.9.3b)
# 18650 Li-ion Battery: CC-BY Dr Kristofer Chan, King's College London/Remote-research.org
circuit board: 8.46667cm x 5.64444cm

parts:
  IC1 = LM324 [package=dil16]
  R = 100 KΩ Resistor [package="0402 [SMD]"]
  R_2 = 100 KΩ Resistor [package="0402 [SMD]"]
  BAT1 = 18650 Li-ion Battery [package=battery-18650]
  R_3 = 100 KΩ Resistor [package="0402 [SMD]"]
  R_4 = 100 KΩ Resistor [package="0402 [SMD]"]

nets:
  N1: IC1.OUT1, R_2.Pin_1
  N2: IC1.IN1-, R_2.Pin_0, R_4.Pin_1
  N3: IC1.IN1+, R.Pin_1, R_3.Pin_0
  N4: R.Pin_0, BAT1.+
  N5: BAT1.-, R_4.Pin_0
  GND: R_3.Pin_1

custom parts:
  LM324: LM324 Quad OpAmp
  100 KΩ Resistor: Resistor Basic schematic elements and footprints for 0603, 1206, and PTH resistors.
  18650 Li-ion Battery: 18650 li-ion Battery Standard 18650 battery with interactive connectors Creative Common Attribution 4.0 International (CC-BY 4.0) license. Any use of this part requires attribution of Dr Kristofer Chan, Department of Geography, King's College London. Contact kristofer.chan [at] kcl.ac.uk OR kris [at] remote-research.org for further information.
