# Fritzing sketch Mesure Vol2 (saved by Fritzing 0.9.3b)

parts:
  IC1 = LM324 [package=dil16]
  R = 100 KΩ Resistor [package="0402 [SMD]"]
  R_2 = 100 KΩ Resistor [package="0402 [SMD]"]
  R_3 = 100 KΩ Resistor [package="0402 [SMD]"]

nets:
  N1: IC1.OUT1, R_2.Pin_1
  N2: IC1.IN1-, R.Pin_1, R_2.Pin_0, R_3.Pin_0
  GND: IC1.IN1+
  -3.7V: R.Pin_0
  volt_measur_1: R_3.Pin_1

custom parts:
  LM324: LM324 Quad OpAmp
  100 KΩ Resistor: Resistor Basic schematic elements and footprints for 0603, 1206, and PTH resistors.
