# Fritzing sketch Mesure Vol3 (saved by Fritzing 0.9.3b)

parts:
  IC1 = LM324 [package=dil16]
  R = 100 KΩ Resistor [package="0402 [SMD]"]
  R_2 = 100 KΩ Resistor [package="0402 [SMD]"]

nets:
  N1: IC1.OUT1, R_2.Pin_1
  N2: IC1.IN1-, R.Pin_1, R_2.Pin_0
  GND: IC1.IN1+
  volt_measur_2: R.Pin_0

custom parts:
  LM324: LM324 Quad OpAmp
  100 KΩ Resistor: Resistor Basic schematic elements and footprints for 0603, 1206, and PTH resistors.
