# Fritzing sketch Mesure vol4 (saved by Fritzing 0.9.3b)

parts:
  R = 100 KΩ Resistor [package="0402 [SMD]"]
  R_2 = 100 KΩ Resistor [package="0402 [SMD]"]
  vOffset = 2.1mm Barrel Jack with Terminal Block
  C1 = Capacitor [package=cap-pth-small2]

nets:
  N1: R.Pin_0, R_2.Pin_1, C1.2
  N2: R.Pin_1, vOffset.POS
  GND: R_2.Pin_0
  volt_measur_3: C1.1

custom parts:
  100 KΩ Resistor: Resistor Basic schematic elements and footprints for 0603, 1206, and PTH resistors.
