# Fritzing sketch scratch fritzing (saved by Fritzing 0.9.3b)
# 18650 Li-ion Battery: CC-BY Dr Kristofer Chan, King's College London/Remote-research.org
perfboards: 1

parts:
  IC1 = LM324 [package=dil16]
  R3 = 100 KΩ Resistor [package="0402 [SMD]"]
  R3_2 = 100 KΩ Resistor [package="0402 [SMD]"]
  12V = 2.1mm Barrel Jack with Terminal Block
  BAT1 = 18650 Li-ion Battery [package=battery-18650]
  R4 = 100 KΩ Resistor [package="0402 [SMD]"]
  R1 = 100 KΩ Resistor [package="0402 [SMD]"]

nets:
  N1: IC1.OUT1, R3_2.Pin_1
  N2: IC1.IN1-, R3_2.Pin_0, R4.Pin_1
  N3: IC1.IN1+, R3.Pin_1, R1.Pin_0
  N4: IC1.V+, 12V.NEG
  N5: IC1.GND, 12V.POS
  N6: R3.Pin_0, BAT1.+
  N7: BAT1.-, R4.Pin_0
  GND: R1.Pin_1

custom parts:
  LM324: LM324 Quad OpAmp
  100 KΩ Resistor: Resistor Basic schematic elements and footprints for 0603, 1206, and PTH resistors.
  18650 Li-ion Battery: 18650 li-ion Battery Standard 18650 battery with interactive connectors Creative Common Attribution 4.0 International (CC-BY 4.0) license. Any use of this part requires attribution of Dr Kristofer Chan, Department of Geography, King's College London. Contact kristofer.chan [at] kcl.ac.uk OR kris [at] remote-research.org for further information.
