# Fritzing sketch whole project (saved by Fritzing 0.9.3b)
# 18650 Li-ion Battery: CC-BY Dr Kristofer Chan, King's College London/Remote-research.org

parts:
  U1 = opa548
  J1 = STM32 Nucleo boards
  R1 = 100 KΩ Resistor [package="0402 [SMD]"]
  R2 = 100 KΩ Resistor [package="0402 [SMD]"]
  R3 = 100 KΩ Resistor [package="0402 [SMD]"]
  R4 = 100 KΩ Resistor [package="0402 [SMD]"]
  R5 = 100 KΩ Resistor [package="0402 [SMD]"]
  R6 = 100 KΩ Resistor [package="0402 [SMD]"]
  BAT1 = 18650 Li-ion Battery [package=battery-18650]
  R_Shunt = 100 KΩ Resistor [package="0402 [SMD]"]
  IC1 = LM324 [package=dil16]
  IC2 = LM324 [package=dil16]
  R8 = 100 KΩ Resistor [package="0402 [SMD]"]
  R9 = 100 KΩ Resistor [package="0402 [SMD]"]
  R10 = 100 KΩ Resistor [package="0402 [SMD]"]
  R11 = 100 KΩ Resistor [package="0402 [SMD]"]
  R13 = 100 KΩ Resistor [package="0402 [SMD]"]
  R14 = 100 KΩ Resistor [package="0402 [SMD]"]
  R15 = 100 KΩ Resistor [package="0402 [SMD]"]
  R18 = 100 KΩ Resistor [package="0402 [SMD]"]
  R19 = 100 KΩ Resistor [package="0402 [SMD]"]
  R21 = 100 KΩ Resistor [package="0402 [SMD]"]  # not connected
  R24 = 100 KΩ Resistor [package="0402 [SMD]"]
  R25 = 100 KΩ Resistor [package="0402 [SMD]"]
  R26 = 100 KΩ Resistor [package="0402 [SMD]"]
  R27 = 100 KΩ Resistor [package="0402 [SMD]"]
  R30 = 100 KΩ Resistor [package="0402 [SMD]"]
  R31 = 100 KΩ Resistor [package="0402 [SMD]"]
  Rdiv1 = 100 KΩ Resistor [package="0402 [SMD]"]
  Rdiv2 = 100 KΩ Resistor [package="0402 [SMD]"]
  C1 = Capacitor [package=cap-pth-small2]
  R22 = 100 KΩ Resistor [package="0402 [SMD]"]
  R26_2 = 100 KΩ Resistor [package="0402 [SMD]"]  # not connected
  R25_2 = 100 KΩ Resistor [package="0402 [SMD]"]  # not connected
  C2 = Capacitor [package=cap-pth-small2]
  V1 = DC Power [voltage=3.7]

nets:
  N1: U1.connector5, R2.Pin_1, R5.Pin_1
  N2: U1.connector7, R1.Pin_0, R3.Pin_1
  N3: U1.connector9, R6.Pin_0
  N4: J1.A0, C1.2, R22.Pin_1
  N5: J1.A1, C2.2
  N6: J1.3V3, Rdiv1.Pin_0
  N7: J1.PA4, R3.Pin_0
  N8: R1.Pin_1, R5.Pin_0, BAT1.+, R11.Pin_0
  N9: R2.Pin_0, R4.Pin_1
  N10: R4.Pin_0, Rdiv1.Pin_1, Rdiv2.Pin_0
  N11: BAT1.-, R_Shunt.Pin_0, R8.Pin_0
  GND: R_Shunt.Pin_1, Rdiv2.Pin_1
  N12: IC1.OUT1, R19.Pin_1, C1.1
  N13: IC1.IN1-, R18.Pin_1
  N14: IC1.OUT3, R14.Pin_1, R18.Pin_0
  N15: IC1.IN3-, R13.Pin_1, R15.Pin_1
  N16: IC1.IN3+, R14.Pin_0
  N17: IC1.IN4-, R8.Pin_1, R9.Pin_1
  N18: IC1.OUT4, R9.Pin_0
  N19: IC2.OUT3, R30.Pin_0, C2.1
  N20: IC2.IN3-, R30.Pin_1, R31.Pin_1
  N21: IC2.IN4+, R24.Pin_1, R25.Pin_0
  N22: IC2.IN4-, R26.Pin_0, R27.Pin_1
  N23: IC2.OUT4, R26.Pin_1, R31.Pin_0
  N24: R10.Pin_1, R11.Pin_1
  N25: R25.Pin_1, V1.V+

custom parts:
  100 KΩ Resistor: Resistor Basic schematic elements and footprints for 0603, 1206, and PTH resistors.
  18650 Li-ion Battery: 18650 li-ion Battery Standard 18650 battery with interactive connectors Creative Common Attribution 4.0 International (CC-BY 4.0) license. Any use of this part requires attribution of Dr Kristofer Chan, Department of Geography, King's College London. Contact kristofer.chan [at] kcl.ac.uk OR kris [at] remote-research.org for further information.
  LM324: LM324 Quad OpAmp
